// Logisim project aiAlu.circ as structural Verilog: 14 circuits, main circuit Half Adder
module Half_Adder (
  input  A,
  input  B,
  output S,
  output C
);

  xor xor_1 (S, A, B);
  and and_1 (C, A, B);
endmodule

module Full_Adder (
  input  C0,
  input  A,
  input  B,
  output S,
  output C1
);

  wire and_1_out, and_2_out, and_3_out, xor_1_out;

  xor xor_1 (xor_1_out, B, A);
  xor xor_2 (S, xor_1_out, C0);
  and and_1 (and_1_out, A, C0);
  and and_2 (and_2_out, B, A);
  and and_3 (and_3_out, B, C0);
  or or_1 (C1, and_1_out, and_2_out, and_3_out);
endmodule

module aiLogic (
  input  [7:0] in_1,
  input  [7:0] in_2
);
endmodule

module a_b (
  input  [7:0] in_1,
  input  [7:0] in_2,
  output [7:0] out_3
);

  and and_1 (out_3[7], in_2[7], in_1[7]);
  and and_2 (out_3[4], in_2[4], in_1[4]);
  and and_3 (out_3[5], in_2[5], in_1[5]);
  and and_4 (out_3[6], in_2[6], in_1[6]);
  and and_5 (out_3[1], in_2[1], in_1[1]);
  and and_6 (out_3[3], in_2[3], in_1[3]);
  and and_7 (out_3[2], in_2[2], in_1[2]);
  and and_8 (out_3[0], in_2[0], in_1[0]);
endmodule

module a__b (
  input  [7:0] in_1,
  input  [7:0] in_2,
  output [7:0] out_3
);

  or or_1 (out_3[7], in_2[7], in_1[7]);
  or or_2 (out_3[4], in_2[4], in_1[4]);
  or or_3 (out_3[5], in_2[5], in_1[5]);
  or or_4 (out_3[6], in_2[6], in_1[6]);
  or or_5 (out_3[3], in_2[3], in_1[3]);
  or or_6 (out_3[1], in_2[1], in_1[1]);
  or or_7 (out_3[2], in_2[2], in_1[2]);
  or or_8 (out_3[0], in_2[0], in_1[0]);
endmodule

module notA (
  input  [7:0] in_1,
  output [7:0] out_2
);

  not not_1 (out_2[7], in_1[7]);
  not not_2 (out_2[5], in_1[5]);
  not not_3 (out_2[3], in_1[3]);
  not not_4 (out_2[6], in_1[6]);
  not not_5 (out_2[0], in_1[0]);
  not not_6 (out_2[2], in_1[2]);
  not not_7 (out_2[4], in_1[4]);
  not not_8 (out_2[1], in_1[1]);
endmodule

module notB (
  input  [7:0] in_1,
  output [7:0] out_2
);

  not not_1 (out_2[7], in_1[7]);
  not not_2 (out_2[1], in_1[1]);
  not not_3 (out_2[6], in_1[6]);
  not not_4 (out_2[3], in_1[3]);
  not not_5 (out_2[4], in_1[4]);
  not not_6 (out_2[0], in_1[0]);
  not not_7 (out_2[2], in_1[2]);
  not not_8 (out_2[5], in_1[5]);
endmodule

module AxorB (
  input  [7:0] in_1,
  input  [7:0] in_2,
  output [7:0] out_3
);

  xor xor_1 (out_3[7], in_2[7], in_1[7]);
  xor xor_2 (out_3[5], in_2[5], in_1[5]);
  xor xor_3 (out_3[6], in_2[6], in_1[6]);
  xor xor_4 (out_3[4], in_2[4], in_1[4]);
  xor xor_5 (out_3[3], in_2[3], in_1[3]);
  xor xor_6 (out_3[2], in_2[2], in_1[2]);
  xor xor_7 (out_3[1], in_2[1], in_1[1]);
  xor xor_8 (out_3[0], in_2[0], in_1[0]);
endmodule

module Adder_8_bit (
  input  [7:0] A,
  input  [7:0] B,
  output C,
  output [7:0] S
);

  wire c1, full_adder_1_c1, full_adder_2_c1, full_adder_3_c1, full_adder_4_c1, full_adder_5_c1,
       half_adder_1_c;

  Half_Adder half_adder_1 (.S(S[0]), .C(half_adder_1_c), .A(A[0]), .B(B[0]));
  Full_Adder full_adder_1 (.S(S[4]), .C1(full_adder_1_c1), .C0(c1), .A(A[4]), .B(B[4]));
  Full_Adder full_adder_2 (.S(S[1]), .C1(full_adder_2_c1), .C0(half_adder_1_c), .A(A[1]), .B(B[1]));
  Full_Adder full_adder_3 (.S(S[5]), .C1(full_adder_3_c1), .C0(full_adder_1_c1), .A(A[5]), .B(B[5]));
  Full_Adder full_adder_4 (.S(S[2]), .C1(full_adder_4_c1), .C0(full_adder_2_c1), .A(A[2]), .B(B[2]));
  Full_Adder full_adder_5 (.S(S[6]), .C1(full_adder_5_c1), .C0(full_adder_3_c1), .A(A[6]), .B(B[6]));
  Full_Adder full_adder_6 (.S(S[3]), .C1(c1), .C0(full_adder_4_c1), .A(A[3]), .B(B[3]));
  Full_Adder full_adder_7 (.S(S[7]), .C1(C), .C0(full_adder_5_c1), .A(A[7]), .B(B[7]));

  // Other names for the same wires on the sheet: _0 = S[0]; _1 = S[1]; _2 = S[2]; _3 = S[3]

  // Notes on the sheet:
  //   HA= Half Adder
  //   FA= Full Adder
endmodule

module Half_Subtractor (
  input  A,
  input  B,
  output D,
  output B_2
);

  wire not_1_out;

  not not_1 (not_1_out, A);
  xor xor_1 (D, A, B);
  and and_1 (B_2, B, not_1_out);
endmodule

module Full_Subtractor (
  input  b0,
  input  A,
  input  B,
  output D,
  output B_2
);

  wire and_1_out, and_2_out, not_1_out, not_2_out, xor_1_out;

  not not_1 (not_1_out, A);
  xor xor_1 (xor_1_out, B, A);
  not not_2 (not_2_out, xor_1_out);
  and and_1 (and_1_out, B, not_1_out);
  xor xor_2 (D, xor_1_out, b0);
  and and_2 (and_2_out, b0, not_2_out);
  or or_1 (B_2, and_2_out, and_1_out);
endmodule

module Subtract_8_bit (
  input  [7:0] A,
  input  [7:0] B,
  output B_2,
  output [7:0] D
);

  wire b1, full_subtractor_1_b_2, full_subtractor_2_b_2, full_subtractor_3_b_2, full_subtractor_4_b_2,
       full_subtractor_5_b_2, half_subtractor_1_b_2;

  Half_Subtractor half_subtractor_1 (.D(D[0]), .B_2(half_subtractor_1_b_2), .A(A[0]), .B(B[0]));
  Full_Subtractor full_subtractor_1 (.D(D[4]), .B_2(full_subtractor_1_b_2), .b0(b1), .A(A[4]), .B(B[4]));
  Full_Subtractor full_subtractor_2 (
    .D(D[1]), .B_2(full_subtractor_2_b_2), .b0(half_subtractor_1_b_2), .A(A[1]), .B(B[1]));
  Full_Subtractor full_subtractor_3 (
    .D(D[5]), .B_2(full_subtractor_3_b_2), .b0(full_subtractor_1_b_2), .A(A[5]), .B(B[5]));
  Full_Subtractor full_subtractor_4 (
    .D(D[2]), .B_2(full_subtractor_4_b_2), .b0(full_subtractor_2_b_2), .A(A[2]), .B(B[2]));
  Full_Subtractor full_subtractor_5 (
    .D(D[6]), .B_2(full_subtractor_5_b_2), .b0(full_subtractor_3_b_2), .A(A[6]), .B(B[6]));
  Full_Subtractor full_subtractor_6 (.D(D[3]), .B_2(b1), .b0(full_subtractor_4_b_2), .A(A[3]), .B(B[3]));
  Full_Subtractor full_subtractor_7 (.D(D[7]), .B_2(B_2), .b0(full_subtractor_5_b_2), .A(A[7]), .B(B[7]));

  // Other names for the same wires on the sheet: _0 = D[0]; _1 = D[1]; _2 = D[2]; _3 = D[3]
endmodule

module Compl_at_2 (
  input  [7:0] N,
  output [7:0] minus_N
);

  wire [7:0] not_8_out;

  not not_1 (not_8_out[7], N[7]);
  not not_2 (not_8_out[2], N[2]);
  not not_3 (not_8_out[4], N[4]);
  not not_4 (not_8_out[1], N[1]);
  not not_5 (not_8_out[3], N[3]);
  not not_6 (not_8_out[6], N[6]);
  not not_7 (not_8_out[5], N[5]);
  not not_8 (not_8_out[0], N[0]);
  _1 u_1_1 (.A(not_8_out), .S(minus_N));
endmodule

module _1 (
  input  [7:0] A,
  output [7:0] S
);

  wire c1, full_adder_1_c1, full_adder_2_c1, full_adder_3_c1, full_adder_4_c1, full_adder_5_c1,
       half_adder_1_c;

  Half_Adder half_adder_1 (.S(S[0]), .C(half_adder_1_c), .A(A[0]), .B(1'b1));
  Full_Adder full_adder_1 (.S(S[4]), .C1(full_adder_1_c1), .C0(c1), .A(A[4]), .B(1'b0));
  Full_Adder full_adder_2 (.S(S[1]), .C1(full_adder_2_c1), .C0(half_adder_1_c), .A(A[1]), .B(1'b0));
  Full_Adder full_adder_3 (.S(S[5]), .C1(full_adder_3_c1), .C0(full_adder_1_c1), .A(A[5]), .B(1'b0));
  Full_Adder full_adder_4 (.S(S[2]), .C1(full_adder_4_c1), .C0(full_adder_2_c1), .A(A[2]), .B(1'b0));
  Full_Adder full_adder_5 (.S(S[6]), .C1(full_adder_5_c1), .C0(full_adder_3_c1), .A(A[6]), .B(1'b0));
  Full_Adder full_adder_6 (.S(S[3]), .C1(c1), .C0(full_adder_4_c1), .A(A[3]), .B(1'b0));
  Full_Adder full_adder_7 (.S(S[7]), .C0(full_adder_5_c1), .A(A[7]), .B(1'b0));  // open: C1

  // Other names for the same wires on the sheet: _6 = A[6]; _7 = A[7]; _0 = S[0]; _1 = S[1]; _2 = S[2]; _3 = S[3]
endmodule
